# Fritzing sketch Wiring Diagram (saved by Fritzing 1.0.7)

parts:
  Part1 = Arduino MKR NB 1500
  BAT1 = 12 battery [package=battery]
  Part2 = Solar Panel [package="Renogy 50 Watts 12 Volt Monocrystalline Bendable Solar Panel"]
  U1 = DFRobot Gravity SEN0262 Current to Voltage Converter [part_number=SEN0262]
  S1 = Gravity KIT0139 Submersible Pressure Level Sensor - Probe
  LTC1 = LTC3780 Step-Up & Step-Down power supply
  U2 = SOLPERK 12V 10A Waterproof Solar Charge Controller
  J2 = Wago 221-413
  J3 = Wago 221-415
  U3 = 12V/24V to 5V 3A Enclosed Micro-USB Converter
  S3 = Taiway 100-SP-X-T1 SPDT Miniature Toggle Switch [part_number=100-SP-X-T1-0-0-B1-M1 package=THT]
  J4 = Wago 221-413

nets:
  GND: Part1.GND, U1.GND
  N1: Part1.A2, U1.SIGNAL
  +3V3: Part1.+3V3, U1.VCC
  N2: BAT1.-, LTC1.VIN-, U2.BATTERY-, J3.Pin_1, J3.Pin_3, J3.Pin_4, J3.Pin_5, U3.IN-
  N3: BAT1.+, U2.BATTERY+, J2.Pin_1, J2.Pin_2, J2.Pin_3, S3.L1
  N4: Part2.Connector_1, U2.SOLAR+
  N5: Part2.Connector_2, U2.SOLAR-
  N6: U1.I+, LTC1.VOUT+
  N7: U1.I-, S1.VCC_(red_+)
  N8: S1.GND_(black_-), LTC1.VOUT-
  N9: LTC1.VIN+, U3.IN+, S3.L2, J4.Pin_1, J4.Pin_2, J4.Pin_3

notes:
  Connect Signal Wire to A2

custom parts:
  Arduino MKR NB 1500: Add Narrowband communication to your project with the MKR NB 1500. It's the perfect choice for devices in remote locations without an Internet connection, or in situations in which power isn't available like on-field deployments, remote metering systems, solar-powered devices, or other extreme scenarios. The board's main processor is a low power Arm® Cortex®-M0 32-bit SAMD21, like in the other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
  12 battery: 12V lead acid type battery, like the Husqvarna YTH2448 12V 35AH battery. This is the mini version 1/4 the size of the actual battery to be closer to typical breadboard parts (around 2in wide rathher than 7in). The pads in pcb are sized to accomidate up to 14ga wire (as these batterys will deliver high currents.)
  Solar Panel: Renogy 50 Watts 12 Volt Solar Panel
  DFRobot Gravity SEN0262 Current to Voltage Converter: DFRobot SEN0262 assembled cable-connected module. Supply 3.3-5.5 V; input 0-25 mA DC; output 0-3 V; 120 ohm termination; board 30 x 22 mm. Five independent terminals; I- is not directly tied to GND. Breadboard and schematic use only; PCB routing intentionally suppressed. Artwork is illustrative, not a fabrication drawing.
  Gravity KIT0139 Submersible Pressure Level Sensor - Probe: Probe from DFRobot KIT0139 kit; use with a separate SEN0262 converter. Two-wire 4-20 mA current-loop sensor; range 0-5 m; operating voltage 12-36 V. Red = positive, black = negative. Thick red air tube is NOT an electrical terminal. Body 108 mm long, 28 mm diameter; strain relief 50 mm; 5 m cable drawn shortened. Breadboard and schematic only; PCB routing suppressed. No circuit simulation.
  LTC3780 Step-Up & Step-Down power supply: The LTC3780 power supply converts DC IN 5-32V to DC OUT 1-30V with max. current of 7 amps permanently (peak 10 amps). Undervoltage shutdown level, constant output current and voltage output level are configurable.
  SOLPERK 12V 10A Waterproof Solar Charge Controller: SOLPERK 12V/10A controller, ASIN B0GMHMLNH9. Four terminals: solar positive/negative and battery positive/negative. Housing approximately 80 x 70 x 22 mm from supplied image. Cable lengths compacted for diagrams. SAE contact orientation drawn from supplied front-view image; polarity follows red/black leads. No internal buses or electrical simulation. PCB suppressed. Unofficial custom part.
  Wago 221-413: Wago 221-413 3 position splicing connector 12AWG.
  Wago 221-415: Wago 221-415 5 position splicing connector 12AWG.
  12V/24V to 5V 3A Enclosed Micro-USB Converter: 15 W enclosed DC-DC converter based on user-supplied PlusRoc photographs. Housing top view 46 x 27 mm; nominal depth 14 mm from related variant drawing. Input red positive and black negative. Micro-USB output represented by two conceptual power terminals only: 5 V and output return. USB data/ID wiring and internal common-ground topology are not documented and are not modeled. PCB routing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
